# Fritzing sketch Esquema_v3 (saved by Fritzing 0.9.3b)
breadboards: 1

parts:
  R1 = Resistor [tolerance=±5% resistance=220 package=THT]
  U2 = NodeMCU V3.0
  Componente1 = HC-SR501 Body Sensor Module
  Componente2 = HC-SR501 Body Sensor Module
  Power_plug1 = Power plug
  J1 = Camdenboss CTB0158-3 [part_number=CTB0158-3 package=THT]
  Q2 = NPN-Transistor [package="TO92 [THT]"]
  LED10 = LED - 5mm [color="Blue (505nm)" package="5 mm [THT]"]
  LED11 = LED - 5mm [color="Green (570nm)" package="5 mm [THT]"]
  LED12 = LED - 5mm [color="Red (633nm)" package="5 mm [THT]"]
  LED13 = LED - 5mm [color="White (4500K)" package="5 mm [THT]"]
  R4 = Resistor [tolerance=±5% resistance=220 package=THT]
  D5 = Rectifier Diode [part_number=1N4001 package="300 mil [THT]"]
  D6 = Rectifier Diode [part_number=1N4001 package="300 mil [THT]"]
  R3 = Resistor [tolerance=±5% resistance=1M package=THT]
  LED14 = RGB LED (com. cathode, rgb) [package="5 mm [THT]"]
  R5 = Resistor [tolerance=±5% resistance=220 package=THT]
  J2 = Camdenboss CTB0158-5 [part_number=CTB0158-5 package=THT]
  J3 = Camdenboss CTB0158-10 [part_number=CTB0158-10 package=THT]  # not connected

nets:
  N1: R1.Pin_0, U2.D2
  N2: R1.Pin_1, LED14.green_anode
  N3: U2.D0, R4.Pin_1
  N4: U2.D1, D5.cathode, D6.cathode, R3.Pin_0
  VCC: Componente1.VCC, Componente2.VCC, J2.pin3
  N5: Componente1.OUT, J2.pin2
  GND: Componente1.GND, Componente2.GND, J2.pin5
  N6: Componente2.OUT, J2.pin1
  N7: Power_plug1.GND, J1.pin1, LED14.common_cathode, J2.terminal_3
  N8: Power_plug1.VCC, R5.Pin_0, J2.terminal_5
  N9: J1.pin2, LED10.cathode, LED11.cathode, LED12.cathode, LED13.cathode
  N10: J1.terminal_1, Q2.E
  N11: J1.terminal_2, Q2.B
  N12: J1.terminal_3, Q2.C, R4.Pin_0
  N13: LED10.anode, LED11.anode, LED12.anode, LED13.anode
  N14: D5.anode, J2.terminal_2
  N15: D6.anode, J2.terminal_1
  N16: LED14.red_anode, R5.Pin_1

notes:
  PIR1
  PIR2
  +Vcc
  GND
  Tira +
  Tira -
  Trans Emi
  Trans Colec
  Trans Base
  Trans Pin

custom parts:
  NodeMCU V3.0: ESP8266 based NodeMCU
  HC-SR501 Body Sensor Module: Pyroelectric Infrared PIR Motion Sensor Detector Module
