# Fritzing sketch Esquema_SinNodeMCU_v1 (saved by Fritzing 0.9.3b)
breadboards: 1

parts:
  R1 = Resistor [tolerance=±5% resistance=220 package=THT]
  Componente1 = HC-SR501 Body Sensor Module
  Componente2 = HC-SR501 Body Sensor Module
  Power_plug1 = Power plug
  J1 = Camdenboss CTB0158-3 [part_number=CTB0158-3 package=THT]
  Q2 = NPN-Transistor [package="TO92 [THT]"]
  LED10 = LED - 5mm [color="Blue (505nm)" package="5 mm [THT]"]
  LED11 = LED - 5mm [color="Green (570nm)" package="5 mm [THT]"]
  LED12 = LED - 5mm [color="Red (633nm)" package="5 mm [THT]"]
  LED13 = LED - 5mm [color="White (4500K)" package="5 mm [THT]"]
  R4 = Resistor [tolerance=±5% resistance=220 package=THT]
  D5 = Rectifier Diode [part_number=1N4001 package="300 mil [THT]"]
  D6 = Rectifier Diode [part_number=1N4001 package="300 mil [THT]"]
  LED14 = RGB LED (com. cathode, rgb) [package="5 mm [THT]"]
  R5 = Resistor [tolerance=±5% resistance=220 package=THT]
  J2 = Camdenboss CTB0158-5 [part_number=CTB0158-5 package=THT]

nets:
  N1: R1.Pin_0, R4.Pin_1, D5.cathode, D6.cathode
  N2: R1.Pin_1, LED14.green_anode
  VCC: Componente1.VCC, Componente2.VCC, J2.pin3
  N3: Componente1.OUT, J2.pin2
  GND: Componente1.GND, Componente2.GND, J2.pin5
  N4: Componente2.OUT, J2.pin1
  N5: Power_plug1.GND, LED14.common_cathode, J2.terminal_3
  N6: Power_plug1.VCC, R5.Pin_0, J2.terminal_5
  N7: J1.pin2, LED10.cathode, LED11.cathode, LED12.cathode, LED13.cathode
  N8: J1.terminal_1, Q2.E
  N9: J1.terminal_2, Q2.B
  N10: J1.terminal_3, Q2.C, R4.Pin_0
  N11: LED10.anode, LED11.anode, LED12.anode, LED13.anode
  N12: D5.anode, J2.terminal_2
  N13: D6.anode, J2.terminal_1
  N14: LED14.red_anode, R5.Pin_1

custom parts:
  HC-SR501 Body Sensor Module: Pyroelectric Infrared PIR Motion Sensor Detector Module
